# Fritzing sketch button_box (saved by Fritzing 0.9.4)

parts:
  S1 = Toggle Switch spst [package=THT]
  S2 = Toggle Switch spst [package=THT]
  BT3 = Arcade Button (red)
  BT2 = Arcade Button (red)
  BT1 = Arcade Button (red)
  BT4 = Arcade Button (blue)
  BT5 = Arcade Button (blue)
  BT6 = Arcade Button (blue)
  R1 = Resistor [tolerance=±5% resistance=10k package="1206 [SMD]"]
  R2 = Resistor [tolerance=±5% resistance=10k package="1206 [SMD]"]
  LED1 = LED - 5mm [color="Red (633nm)" package="5 mm [THT]"]
  J1 = Piezo Speaker
  LE3 = LED - 5mm [color="Red (633nm)" package="5 mm [THT]"]
  LED2 = LED - 5mm [color="Red (633nm)" package="5 mm [THT]"]
  LED5 = LED - 5mm [color="Blue (525nm)" package="5 mm [THT]"]
  LED6 = LED - 5mm [color="Blue (525nm)" package="5 mm [THT]"]
  LED4 = LED - 5mm [color="Blue (525nm)" package="5 mm [THT]"]
  LED7 = LED - 5mm [color="Red (633nm)" part_number="internally connected" package="5 mm [THT]"]
  LED8 = LED - 5mm [color="Blue (525nm)" part_number=not_enough_gpio package="5 mm [THT]"]
  VCC1 = 4 x AAA Battery Mount
  S3 = Toggle Switch spst [package=THT]
  Bauteil2 = 0.56" 7-segment LED Backpack [part_number=879]
  C1 = Capacitor Polarized [part_number=1000uF package=panasonic_e]
  R4 = Resistor [tolerance=±5% resistance=1k package="1206 [SMD]"]
  R5 = Resistor [tolerance=±5% resistance=1k package="1206 [SMD]"]
  Bauteil4 = PowerBoost 1000 Basic [part_number="Pololu U1V11F5"]
  R9 = Resistor [tolerance=±5% resistance=100 package=THT]
  R10 = Resistor [tolerance=±5% resistance=100 package=THT]
  R11 = Resistor [tolerance=±5% resistance=100 package=THT]
  JOY1 = Adafruit Arcade Joystick
  Bauteil3 = 16 NeoPixel Ring [part_number=1463]
  R12 = Resistor [tolerance=±5% resistance=100 package=THT]
  R13 = Resistor [tolerance=±5% resistance=100 package=THT]
  R14 = Resistor [tolerance=±5% resistance=100 package=THT]
  R15 = Resistor [tolerance=±5% resistance=100 package=THT]
  ATMEGA2560Pro = Mega2560 R3 Pro ch340g
  Bauteil5 = NRF24L01+ Breakout Board
  IC1 = V_REG_LD1117VXX [package=78xxl]
  C2 = Capacitor [part_number=150uF package=cap-pth-small]

nets:
  GND: S1.L1, S2.L1, BT3.no_name_yet#2, BT2.no_name_yet#2, BT1.no_name_yet#2, BT4.no_name_yet#2, BT5.no_name_yet#2, BT6.no_name_yet#2, LED1.cathode, J1.pin2, LE3.cathode, LED2.cathode, LED5.cathode, LED6.cathode, LED4.cathode, LED7.cathode, LED8.cathode, VCC1.-, Bauteil2.GND, C1.-, Bauteil4.GND, JOY1.COM, Bauteil3.GND, ATMEGA2560Pro.GND, Bauteil5.GND, IC1.GND, C2.2
  N1: S1.COM, R1.Pin_1, ATMEGA2560Pro.23
  N2: S2.COM, R2.Pin_1, ATMEGA2560Pro.24
  N3: BT3.no_name_yet#1, ATMEGA2560Pro.30
  N4: BT2.no_name_yet#1, ATMEGA2560Pro.29
  N5: BT1.no_name_yet#1, ATMEGA2560Pro.28
  N6: BT4.no_name_yet#1, ATMEGA2560Pro.25
  N7: BT5.no_name_yet#1, ATMEGA2560Pro.26
  N8: BT6.no_name_yet#1, ATMEGA2560Pro.27
  5V: R1.Pin_0, R2.Pin_0, Bauteil2.VDD, C1.+, Bauteil4.5.0V, Bauteil3.VDD, ATMEGA2560Pro.VTG, ATMEGA2560Pro.5V, IC1.IN
  N9: LED1.anode, R9.Pin_1
  N10: J1.pin1, R12.Pin_0
  N11: LE3.anode, R14.Pin_1
  N12: LED2.anode, R13.Pin_1
  N13: LED5.anode, R11.Pin_1
  N14: LED6.anode, R10.Pin_1
  N15: LED4.anode, R15.Pin_1
  N16: LED7.anode, ATMEGA2560Pro.9▀
  N17: LED8.anode, ATMEGA2560Pro.8▀
  N18: VCC1.+, S3.COM
  N19: S3.L1, Bauteil4.VBAT
  N20: Bauteil2.SCL, ATMEGA2560Pro.21
  N21: Bauteil2.SDA, ATMEGA2560Pro.20
  N22: R4.Pin_0, R5.Pin_0, ATMEGA2560Pro.22
  N23: R4.Pin_1, R5.Pin_1, Bauteil3.IN
  N24: R9.Pin_0, ATMEGA2560Pro.2▀
  N25: R10.Pin_0, ATMEGA2560Pro.6▀
  N26: R11.Pin_0, ATMEGA2560Pro.4▀
  N27: JOY1.N, ATMEGA2560Pro.32
  N28: JOY1.S, ATMEGA2560Pro.33
  N29: JOY1.W, ATMEGA2560Pro.34
  N30: JOY1.E, ATMEGA2560Pro.35
  N31: R12.Pin_1, ATMEGA2560Pro.10▀
  N32: R13.Pin_0, ATMEGA2560Pro.5▀
  N33: R14.Pin_0, ATMEGA2560Pro.7▀
  N34: R15.Pin_0, ATMEGA2560Pro.3▀
  N35: ATMEGA2560Pro.11▀, Bauteil5.IRQ
  N36: ATMEGA2560Pro.49, Bauteil5.CE
  N37: ATMEGA2560Pro.51/MOSI, Bauteil5.MOSI
  N38: ATMEGA2560Pro.53, Bauteil5.CS
  N39: ATMEGA2560Pro.52/SCK, Bauteil5.SCK
  N40: ATMEGA2560Pro.50/MISO, Bauteil5.MISO
  N41: Bauteil5.VCC, IC1.OUT, C2.1

notes:
  Arcade Stick - internal PullUp
  Arcade Buttons - Internal PullUp

custom parts:
  Toggle Switch spst: Toggle Switch single pole single throw
  Arcade Button (red): Adafruit Arcade Button (red)
  Arcade Button (blue): Adafruit Arcade Button (blue)
  0.56" 7-segment LED Backpack: This 0.56" 7-segment LED display includes a driver chip for simple control via an I2C interface. The backpack features address-selection jumpers so you can connect up to eight displays on a single I2C bus.
  PowerBoost 1000 Basic: The PowerBoost 1000 is a little DC/DC boost converter module that can run from 1.8V batteries or higher, and convert the battery output to 5.2V DC for running your 5V projects. At its heart is a TPS61030 boost converter from TI. This boost converter chip has some really nice extras such as low battery detection, 4A internal switch, synchronous conversion, excellent efficiency, and 700KHz high-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
  16 NeoPixel Ring: 16 ultra bright smart LED NeoPixels are arranged in a circle with 1.75" (44.5mm) outer diameter. The rings are 'chainable' - connect the output pin of one to the input pin of another. Use only one microcontroller pin to control as many as you can chain together! Each LED is addressable as the driver chip is inside the LED. Each one has ~18mA constant current drive so the color will be very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
  Mega2560 R3 Pro ch340g: The Mega 2560 R3 Pro Mini :- Completely compatible with original Arduino Mega2560 Pin pitch: 0.1 inch Size: 5.42cm*3.68cm With Atmega16U2 chip as the USB to Serial converter 5V working voltage. Input Voltage:7-12V Analog Input Pins: 16 Digital I/O pins: 54 The Mega 2560 R3 Pro Mini has no datasheet and no info and I don't have one to compare, so I made this based on photos. Dec 2019 modified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
